// Logisim project misc16bit.circ as structural Verilog: 3 circuits, main circuit main
module main (
  input  in_1
);

  wire and_1_out, and_2_out, and_3_out, and_4_out, and_5_out, and_6_out, button_1_out, data_flag,
       data_instr_out, demultiplexer_1_out5, e_D, e_KR, e_R0, e_R1, e_R2, execute, fetch, inc_IAR,
       multiplexer_2_out, s_DAR, s_JAR, s_MAR, s_R0, s_R1, s_R2, write;
  wire [2:0] counter_1_q;
  wire [15:0] adder_1_out, D_q, demultiplexer_2_out0, demultiplexer_2_out1, IAR_q, instr, JAR_q, KR_q, MAR_q,
       multiplexer_1_out, pull_resistor_1_node, R0_q, R1_q, R2_q, ram_1_dout, rom_1_data;

  Pull_Resistor pull_resistor_1 (.node(pull_resistor_1_node));
  Register #(.width(16)) MAR (.D(pull_resistor_1_node), .Q(MAR_q));  // open: en, clk, clr
  // Probe on pull_resistor_1_node
  Counter #(.max('h7), .width(3)) counter_1 (
    .Q(counter_1_q), .clk(button_1_out), .clr(demultiplexer_1_out5));  // open: load, D, count, carry, up
  Button button_1 (.out(button_1_out));
  ROM #(.addrWidth(16), .dataWidth(16)) rom_1 (.addr(IAR_q), .data(rom_1_data));
  RAM #(.addrWidth(16), .dataWidth(16), .trigger("high")) ram_1 (.addr(MAR_q), .dout(ram_1_dout));  // open: we, oe, din
  Demultiplexer #(.select(3)) demultiplexer_1 (
    .out1(fetch), .out2(execute), .out3(write), .out4(inc_IAR), .out5(demultiplexer_1_out5), .in(1'b1),
    .sel(counter_1_q));  // open: out0, out6, out7
  Adder #(.width(16)) adder_1 (.a(16'h1), .b(IAR_q), .out(adder_1_out));  // open: cin, cout
  Multiplexer #(.width(16)) multiplexer_1 (.in0(adder_1_out), .in1(JAR_q), .out(multiplexer_1_out), .sel(in_1));
  Register #(.width(16)) IAR (.D(multiplexer_1_out), .clk(inc_IAR), .Q(IAR_q));  // open: en, clr
  Demultiplexer #(.width(16)) demultiplexer_2 (
    .out0(demultiplexer_2_out0), .out1(demultiplexer_2_out1), .in(rom_1_data), .sel(data_flag));
  Register #(.width(16)) D (.D(demultiplexer_2_out1), .clk(and_1_out), .Q(D_q));  // open: en, clr
  Controlled_Buffer #(.width(16)) controlled_buffer_1 (.in(ram_1_dout), .out(pull_resistor_1_node));  // open: en
  assign pull_resistor_1_node = e_D ? D_q : 16'bz;  // Controlled_Buffer controlled_buffer_2
  and and_1 (and_1_out, fetch, data_flag);
  Register #(.width(16)) R0 (.D(pull_resistor_1_node), .clk(and_2_out), .Q(R0_q));  // open: en, clr
  and and_2 (and_2_out, s_R0, execute);
  assign pull_resistor_1_node = e_R0 ? R0_q : 16'bz;  // Controlled_Buffer controlled_buffer_3
  Register #(.width(16)) IR (.D(demultiplexer_2_out0), .clk(fetch), .Q(instr));  // open: en, clr
  Register #(.width(16)) R1 (.D(pull_resistor_1_node), .clk(and_3_out), .Q(R1_q));  // open: en, clr
  and and_3 (and_3_out, s_R1, execute);
  assign pull_resistor_1_node = e_R1 ? R1_q : 16'bz;  // Controlled_Buffer controlled_buffer_4
  Register #(.width(16)) R2 (.D(pull_resistor_1_node), .clk(and_4_out), .Q(R2_q));  // open: en, clr
  and and_4 (and_4_out, s_R2, execute);
  assign pull_resistor_1_node = e_R2 ? R2_q : 16'bz;  // Controlled_Buffer controlled_buffer_5
  and data_instr (data_instr_out, instr[12], ~instr[13], ~instr[14], ~instr[15]);  // AND_Gate
  Register #(.width(16)) JAR (.D(pull_resistor_1_node), .clk(and_5_out), .Q(JAR_q));  // open: en, clr
  Multiplexer multiplexer_2 (.in0(data_instr_out), .in1(1'b0), .out(multiplexer_2_out), .sel(data_flag));
  and and_5 (and_5_out, s_JAR, execute);
  alu alu_1 (.opcode(instr[15:12]));  // open: x, y, o
  D_Flip_Flop d_ff_1 (.D(multiplexer_2_out), .clk(execute), .Q(data_flag));  // open: Qn, preset, reset
  Register #(.width(16)) KR (.Q(KR_q));  // open: D, en, clk, clr
  assign pull_resistor_1_node = e_KR ? KR_q : 16'bz;  // Controlled_Buffer controlled_buffer_6
  Register #(.width(16)) DAR (.D(pull_resistor_1_node), .clk(and_6_out));  // open: en, Q, clr
  and and_6 (and_6_out, s_DAR, execute);
  control_unit control_unit_1 (
    .instr(instr), .e_D(e_D), .e_R0(e_R0), .e_R1(e_R1), .e_R2(e_R2), .e_KR(e_KR), .s_R0(s_R0), .s_R1(s_R1),
    .s_R2(s_R2), .s_MAR(s_MAR), .s_JAR(s_JAR), .s_DAR(s_DAR));  // open: in_2, in_3

  // Notes on the sheet:
  //   contents of rom_1 (hex, n*v repeats v):
  //   2730
  //   Эта общая шина нужна для того чтобы реализовать команду move
endmodule

module control_unit (
  input  [15:0] instr,
  input  [3:0] in_2,
  input  [3:0] in_3,
  output e_D,
  output e_R0,
  output e_R1,
  output e_R2,
  output e_KR,
  output s_R0,
  output s_R1,
  output s_R2,
  output s_MAR,
  output s_JAR,
  output s_DAR
);

  wire demultiplexer_1_out2, demultiplexer_1_out3, demultiplexer_1_out4, demultiplexer_1_out5,
       demultiplexer_1_out7, demultiplexer_1_out9, demultiplexer_2_out1, demultiplexer_2_out2,
       demultiplexer_2_out3, demultiplexer_2_out4, demultiplexer_2_out8, move_instr;

  and MOVE (move_instr, ~instr[15], ~instr[14], instr[13], ~instr[12]);  // AND_Gate
  Demultiplexer #(.select(4)) demultiplexer_1 (
    .out2(demultiplexer_1_out2), .out3(demultiplexer_1_out3), .out4(demultiplexer_1_out4),
    .out5(demultiplexer_1_out5), .out7(demultiplexer_1_out7), .out9(demultiplexer_1_out9), .in(1'b1),
    .sel(instr[11:8]));  // open: out0, out1, out6, out8, out10, out11, out12, out13, out14, out15
  Demultiplexer #(.select(4)) demultiplexer_2 (
    .out1(demultiplexer_2_out1), .out2(demultiplexer_2_out2), .out3(demultiplexer_2_out3),
    .out4(demultiplexer_2_out4), .out8(demultiplexer_2_out8), .in(1'b1), .sel(instr[7:4]));  // open: out0, out5, out6, out7, out9, out10, out11, out12, out13, out14, out15
  and and_1 (e_D, move_instr, demultiplexer_2_out1);
  and and_2 (e_R0, demultiplexer_2_out2, move_instr);
  and and_3 (e_R1, move_instr, demultiplexer_2_out3);
  and and_4 (e_R2, move_instr, demultiplexer_2_out4);
  and and_5 (e_KR, move_instr, demultiplexer_2_out8);
  and and_6 (s_R0, move_instr, demultiplexer_1_out2);
  and and_7 (s_R1, move_instr, demultiplexer_1_out3);
  and and_8 (s_R2, move_instr, demultiplexer_1_out4);
  and and_9 (s_MAR, move_instr, demultiplexer_1_out5);
  and and_10 (s_JAR, move_instr, demultiplexer_1_out7);
  and and_11 (s_DAR, move_instr, demultiplexer_1_out9);

  // Other names for the same wires on the sheet: dest_reg[3:0] = instr[11:8]; source_reg[3:0] = instr[7:4]

  // Notes on the sheet:
  //   move instruction
endmodule

module alu (
  input  [15:0] x,
  input  [15:0] y,
  input  [3:0] opcode,
  output [15:0] o
);

  wire [15:0] adder_1_out, and_1_out, not_1_out, or_1_out, subtractor_1_out;

  Adder #(.width(16)) adder_1 (.a(x), .b(y), .out(adder_1_out));  // open: cin, cout
  Subtractor #(.width(16)) subtractor_1 (.a(x), .b(y), .out(subtractor_1_out));  // open: bin, bout
  assign and_1_out = x & y;  // AND_Gate and_1, 16 bits wide
  assign or_1_out = x | y;  // OR_Gate or_1, 16 bits wide
  assign not_1_out = ~x;  // NOT_Gate not_1, 16 bits wide
  Multiplexer #(.select(4), .width(16)) multiplexer_1 (
    .in3(adder_1_out), .in4(subtractor_1_out), .in5(and_1_out), .in6(or_1_out), .in7(not_1_out), .out(o),
    .sel(opcode));  // open: in0, in1, in2, in8, in9, in10, in11, in12, in13, in14, in15
endmodule
